# Fritzing sketch rangkaian_test_bench (saved by Fritzing 0.9.10b)
breadboards: 1

parts:
  Part1 = Arduino Nano (Rev3.0)
  OLED_I2C1 = OLED 128x64 I2C Monochrome Display
  Load_Cell1 = Load Cell - Red/white/black/green
  920KV_Motor1 = DJI 920 KV Motor
  M1 = ESC
  Part2 = HX711 Weighing Sensor Module
  U1 = POT [knob_status=50% power=0.5W package=pot_alpha_rv16af-20]
  M2 = fc-51 [package=THT]

nets:
  GND: Part1.GND, OLED_I2C1.GND, M1.GND, Part2.GND, U1.E, M2.pin2
  N1: Part1.D2, Part2.DO/RX
  N2: Part1.D3, Part2.CK/TX
  N3: Part1.D8, M2.pin1
  N4: Part1.D9, M1.DATA
  5V: Part1.5V, OLED_I2C1.VDD, M1.5V, Part2.VCC, U1.A, M2.pin3
  N5: Part1.A5, OLED_I2C1.SCK
  N6: Part1.A4, OLED_I2C1.SDA
  N7: Part1.A0, U1.S
  N8: Load_Cell1.wire1, Part2.E+
  N9: Load_Cell1.wire2, Part2.A-
  N10: Load_Cell1.wire3, Part2.E-
  N11: Load_Cell1.wire4, Part2.A+
  N12: 920KV_Motor1.w, M1.W
  N13: 920KV_Motor1.v, M1.V
  N14: 920KV_Motor1.u, M1.U

notes:
  ESC
  40A
  4-6s Lipo Battery

custom parts:
  Load Cell - Red/white/black/green: A rectangle load cell/weighting pressure Sensor with four wires - Red, white, black, green. Normally corresponding with E+, E-, A+, A- respectively.
  DJI 920 KV Motor: DJI Brushless Outrunner 2212/920K Motor F330-550
  HX711 Weighing Sensor Module: HX711 is a precision 24-bit analog-to-digital converter (ADC) designed for weigh scales and industrial control applications to interface directly with a bridge sensor.
